// Digital circuit frontpanel.dig as structural Verilog
module frontpanel (
  input  clock,
  output [15:0] R0,
  output [15:0] R1,
  output [15:0] R2,
  output [15:0] R3,
  output [3:0] PC,
  output halt,
  output error
);

  wire advance_out, C, control_1_p4, decoder_1_p2, decoder_1_p4, fetch_1_p6, hex, hexdisplay_1_p2,
       hexdisplay_1_p5, hexdisplay_1_p8, hexdisplay_1_p10, hexdisplay_1_p13, hexdisplay_2_p2,
       hexdisplay_2_p5, hexdisplay_2_p8, hexdisplay_2_p10, hexdisplay_2_p13, instrdisplay_1_p1,
       instrdisplay_1_p2, instrdisplay_1_p3, instrdisplay_1_p4, instrdisplay_1_p5, instrdisplay_1_p6, jump,
       memaccess_1_str, pmshim_1_c, pmshim_1_l, pmshim_1_s, rd_valid, regdisplay_1_p1, regdisplay_1_p2,
       regdisplay_2_p1, regdisplay_2_p2, rs_valid, sys, T;
  wire [1:0] control_1_p10, rd, rs;
  wire [2:0] control_1_p5;
  wire [3:0] hexdisplay_1_p1, hexdisplay_1_p4, hexdisplay_1_p6, hexdisplay_1_p9, hexdisplay_1_p12,
       hexdisplay_2_p1, hexdisplay_2_p4, hexdisplay_2_p6, hexdisplay_2_p9, hexdisplay_2_p12, pmshim_1_a;
  wire [4:0] op;
  wire [15:0] Data_d, decoder_1_p1, execute_1_result, instrdisplay_1_d1, instrdisplay_1_d2,
       instrdisplay_1_d3, instrdisplay_1_d4, instrdisplay_1_d5, instrdisplay_1_d6, L, memaccess_1_a,
       memaccess_1_d_in, memaccess_1_wrval, pmshim_1_d, Program_d, R, regdisplay_1_d1, regdisplay_1_d2,
       regdisplay_2_d1, regdisplay_2_d2;

  EEPROMDualPort #(.AddrBits(4), .isProgramMemory("true"), .Bits(16)) Program (
    .A(pmshim_1_a), .Din(pmshim_1_d), .str(pmshim_1_s), .C(pmshim_1_c), .ld(pmshim_1_l), .D(Program_d));
  pmshim pmshim_1 (.pc(PC), .A(pmshim_1_a), .D(pmshim_1_d), .s(pmshim_1_s), .C(pmshim_1_c), .L(pmshim_1_l));
  SixteenSeg sixteenseg_1 (.led(regdisplay_1_d1), .dp(regdisplay_1_p1));
  regdisplay regdisplay_1 (
    .D1(regdisplay_1_d1), .P1(regdisplay_1_p1), .D2(regdisplay_1_d2), .P2(regdisplay_1_p2), .E(1'b1),
    .J(jump), .R(rd));
  // fetch fetch_1: pin names not known; wires that end beside it: Program_d, C, R, jump, PC, fetch_1_p6
  Button advance (.out(advance_out));
  or or_1 (C, advance_out, clock);
  SixteenSeg sixteenseg_2 (.led(regdisplay_1_d2), .dp(regdisplay_1_p2));
  Seven_Seg_Hex seven_seg_hex_1 (.d(hexdisplay_1_p1), .dp(hexdisplay_1_p2));
  Seven_Seg_Hex seven_seg_hex_2 (.d(hexdisplay_1_p4), .dp(hexdisplay_1_p5));
  // hexdisplay hexdisplay_1: pin names not known; wires that end beside it: hexdisplay_1_p1, hexdisplay_1_p2, rd_valid, hexdisplay_1_p4, hexdisplay_1_p5, hexdisplay_1_p6, L, hexdisplay_1_p8, hexdisplay_1_p9, hexdisplay_1_p10, hex, hexdisplay_1_p12, hexdisplay_1_p13
  Seven_Seg_Hex seven_seg_hex_3 (.d(hexdisplay_1_p6), .dp(hexdisplay_1_p8));
  Seven_Seg_Hex seven_seg_hex_4 (.d(hexdisplay_1_p9), .dp(hexdisplay_1_p10));
  // decoder decoder_1: pin names not known; wires that end beside it: decoder_1_p1, decoder_1_p2, fetch_1_p6, decoder_1_p4, rs, rd, L, R, sys, op, rs_valid, rd_valid
  Seven_Seg_Hex seven_seg_hex_5 (.d(hexdisplay_1_p12), .dp(hexdisplay_1_p13));
  SixteenSeg sixteenseg_3 (.led(instrdisplay_1_d1), .dp(instrdisplay_1_p1));
  instrdisplay instrdisplay_1 (
    .D1(instrdisplay_1_d1), .P1(instrdisplay_1_p1), .D2(instrdisplay_1_d2), .P2(instrdisplay_1_p2),
    .D3(instrdisplay_1_d3), .P3(instrdisplay_1_p3), .D4(instrdisplay_1_d4), .P4(instrdisplay_1_p4),
    .D5(instrdisplay_1_d5), .P5(instrdisplay_1_p5), .D6(instrdisplay_1_d6), .P6(instrdisplay_1_p6), .S(sys),
    .I(op));
  SixteenSeg sixteenseg_4 (.led(instrdisplay_1_d2), .dp(instrdisplay_1_p2));
  SixteenSeg sixteenseg_5 (.led(instrdisplay_1_d3), .dp(instrdisplay_1_p3));
  // control control_1: pin names not known; wires that end beside it: sys, op, C, control_1_p4, control_1_p5, T, halt, error, decoder_1_p4, control_1_p10, jump
  SixteenSeg sixteenseg_6 (.led(instrdisplay_1_d4), .dp(instrdisplay_1_p4));
  SixteenSeg sixteenseg_7 (.led(instrdisplay_1_d5), .dp(instrdisplay_1_p5));
  SixteenSeg sixteenseg_8 (.led(instrdisplay_1_d6), .dp(instrdisplay_1_p6));
  Seven_Seg_Hex seven_seg_hex_6 (.d(hexdisplay_2_p1), .dp(hexdisplay_2_p2));
  Seven_Seg_Hex seven_seg_hex_7 (.d(hexdisplay_2_p4), .dp(hexdisplay_2_p5));
  // hexdisplay hexdisplay_2: pin names not known; wires that end beside it: hexdisplay_2_p1, hexdisplay_2_p2, 1'b1, hexdisplay_2_p4, hexdisplay_2_p5, hexdisplay_2_p6, R, hexdisplay_2_p8, hexdisplay_2_p9, hexdisplay_2_p10, hex, hexdisplay_2_p12, hexdisplay_2_p13
  execute execute_1 (.L(L), .R(R), .op(control_1_p5), .result(execute_1_result), .t_in(control_1_p4));
  Seven_Seg_Hex seven_seg_hex_8 (.d(hexdisplay_2_p6), .dp(hexdisplay_2_p8));
  Seven_Seg_Hex seven_seg_hex_9 (.d(hexdisplay_2_p9), .dp(hexdisplay_2_p10));
  DipSwitch u_hex (.out(hex));
  Seven_Seg_Hex seven_seg_hex_10 (.d(hexdisplay_2_p12), .dp(hexdisplay_2_p13));
  memaccess memaccess_1 (
    .result(execute_1_result), .rdval(decoder_1_p1), .mem(decoder_1_p4), .memop(control_1_p10), .D(Data_d),
    .wrval(memaccess_1_wrval), .A(memaccess_1_a), .D_in(memaccess_1_d_in), .str(memaccess_1_str));
  SixteenSeg sixteenseg_9 (.led(regdisplay_2_d1), .dp(regdisplay_2_p1));
  regdisplay regdisplay_2 (
    .D1(regdisplay_2_d1), .P1(regdisplay_2_p1), .D2(regdisplay_2_d2), .P2(regdisplay_2_p2), .E(rs_valid),
    .J(1'b0), .R(rs));
  SixteenSeg sixteenseg_10 (.led(regdisplay_2_d2), .dp(regdisplay_2_p2));
  // regfile regfile_1: pin names not known; wires that end beside it: rs, rd, memaccess_1_wrval, C, decoder_1_p1, decoder_1_p2, R0, R1, R2, R3
  RAMDualPort #(.AddrBits(16), .Bits(16)) Data (
    .A(memaccess_1_a), .Din(memaccess_1_d_in), .str(memaccess_1_str), .C(C), .ld(1'b1), .D(Data_d));
  LED u_T (.in(T));

  // Notes on the sheet:
  //   clock: Hz: 10
  //   contents of Program (hex, n*v repeats v):
  //   303,30b,b13,8092,b11a,1d,810a,b09a,81d,1c,1003,61
  //   rj45 Creates
endmodule
